// Logisim project GM_16x.circ as structural Verilog: 6 circuits, main circuit main
module main (
);

  wire _0, alu_1_zero, and_1_out, b, clk, g, j, lw, or_1_out, sw, undriven;
  wire [3:0] rom_1_instruction, rom_1_instruction_2, rom_1_instruction_3, rom_1_instruction_4, undriven_2;
  wire [15:0] alu_1_out, demultiplexer_1_out0, demultiplexer_1_out1, demultiplexer_2_out0,
       demultiplexer_2_out1, mem_1_dataout, multiplexer_1_out, regs_1_data1, regs_1_data2, regs_1_jumper;

  Clock clock_1 (.out(clk));
  ROM rom_1 (
    .Address(multiplexer_1_out),
    .Instruction({rom_1_instruction, rom_1_instruction_4, rom_1_instruction_3, rom_1_instruction_2}), .gt(g),
    .clk(clk), .clr(_0));
  Regs regs_1 (
    .str(undriven), .rd(rom_1_instruction_4), .in(multiplexer_1_out), .data1(regs_1_data1),
    .data2(regs_1_data2), .rt(rom_1_instruction_2), .clk(clk), .clr(_0), .rs(rom_1_instruction_3),
    .jumper(regs_1_jumper));
  Demultiplexer #(.width(16)) demultiplexer_1 (
    .out0(demultiplexer_1_out0), .out1(demultiplexer_1_out1), .in(alu_1_out), .sel(or_1_out));  // open: en
  ALU alu_1 (
    .ALUop(undriven_2), .out(alu_1_out), .zero(alu_1_zero), .data1(regs_1_data1), .data2(regs_1_data2),
    .immed({4'b0000, rom_1_instruction_4, rom_1_instruction_3, rom_1_instruction_2}), .jumper(regs_1_jumper));
  Multiplexer #(.width(16)) multiplexer_1 (
    .in0(demultiplexer_1_out0), .in1(mem_1_dataout), .out(multiplexer_1_out), .sel(or_1_out));  // open: en
  Multiplexer multiplexer_2 (.in0(j), .in1(and_1_out), .out(g), .sel(b));  // open: en
  and and_1 (and_1_out, j, alu_1_zero);
  Demultiplexer #(.width(16)) demultiplexer_2 (
    .out0(demultiplexer_2_out0), .out1(demultiplexer_2_out1), .in(demultiplexer_1_out1));  // open: sel, en
  or or_1 (or_1_out, sw, lw);
  MEM mem_1 (
    .Address(demultiplexer_2_out0), .DataIn(demultiplexer_2_out1), .DataOut(mem_1_dataout), .sw(sw), .lw(lw));  // open: clk, clr
endmodule

module Regs (
  input  [3:0] rs,
  input  str,
  input  [3:0] rd,
  input  [3:0] rt,
  input  [15:0] in,
  input  clk,
  input  clr,
  output [15:0] data1,
  output [15:0] data2,
  output [15:0] jumper
);

  wire demultiplexer_1_out1, demultiplexer_1_out2, demultiplexer_1_out3, demultiplexer_1_out4,
       demultiplexer_1_out5, demultiplexer_1_out6, demultiplexer_1_out7, demultiplexer_1_out8,
       demultiplexer_1_out9, demultiplexer_1_out10, demultiplexer_1_out11, demultiplexer_1_out12,
       demultiplexer_1_out13, demultiplexer_1_out14, demultiplexer_1_out15;
  wire [15:0] demultiplexer_2_out0, demultiplexer_2_out1, demultiplexer_2_out2, demultiplexer_2_out3,
       demultiplexer_2_out4, demultiplexer_2_out5, demultiplexer_2_out6, demultiplexer_2_out7,
       demultiplexer_2_out8, demultiplexer_2_out9, demultiplexer_2_out10, demultiplexer_2_out11,
       demultiplexer_2_out12, demultiplexer_2_out13, demultiplexer_2_out14, demultiplexer_2_out15,
       register_1_q, register_2_q, register_3_q, register_4_q, register_5_q, register_6_q, register_7_q,
       register_8_q, register_9_q, register_10_q, register_11_q, register_12_q, register_13_q, register_14_q,
       register_15_q;

  Demultiplexer #(.select(4)) demultiplexer_1 (
    .out1(demultiplexer_1_out1), .out2(demultiplexer_1_out2), .out3(demultiplexer_1_out3),
    .out4(demultiplexer_1_out4), .out5(demultiplexer_1_out5), .out6(demultiplexer_1_out6),
    .out7(demultiplexer_1_out7), .out8(demultiplexer_1_out8), .out9(demultiplexer_1_out9),
    .out10(demultiplexer_1_out10), .out11(demultiplexer_1_out11), .out12(demultiplexer_1_out12),
    .out13(demultiplexer_1_out13), .out14(demultiplexer_1_out14), .out15(demultiplexer_1_out15), .in(str),
    .sel(rd));  // open: out0, en
  Demultiplexer #(.select(4), .width(16)) demultiplexer_2 (
    .out0(demultiplexer_2_out0), .out1(demultiplexer_2_out1), .out2(demultiplexer_2_out2),
    .out3(demultiplexer_2_out3), .out4(demultiplexer_2_out4), .out5(demultiplexer_2_out5),
    .out6(demultiplexer_2_out6), .out7(demultiplexer_2_out7), .out8(demultiplexer_2_out8),
    .out9(demultiplexer_2_out9), .out10(demultiplexer_2_out10), .out11(demultiplexer_2_out11),
    .out12(demultiplexer_2_out12), .out13(demultiplexer_2_out13), .out14(demultiplexer_2_out14),
    .out15(demultiplexer_2_out15), .in(in), .sel(rd));  // open: en
  Register #(.width(16)) register_1 (.D(demultiplexer_2_out0), .en(1'b0), .Q(register_1_q), .clk(clk), .clr(clr));
  Register #(.width(16)) register_2 (
    .D(demultiplexer_2_out1), .en(demultiplexer_1_out1), .Q(register_2_q), .clk(clk), .clr(clr));
  Register #(.width(16)) register_3 (
    .D(demultiplexer_2_out2), .en(demultiplexer_1_out2), .Q(register_3_q), .clk(clk), .clr(clr));
  Register #(.width(16)) register_4 (
    .D(demultiplexer_2_out3), .en(demultiplexer_1_out3), .Q(register_4_q), .clk(clk), .clr(clr));
  Register #(.width(16)) register_5 (
    .D(demultiplexer_2_out4), .en(demultiplexer_1_out4), .Q(register_5_q), .clk(clk), .clr(clr));
  Register #(.width(16)) register_6 (
    .D(demultiplexer_2_out5), .en(demultiplexer_1_out5), .Q(register_6_q), .clk(clk), .clr(clr));
  Register #(.width(16)) register_7 (
    .D(demultiplexer_2_out6), .en(demultiplexer_1_out6), .Q(register_7_q), .clk(clk), .clr(clr));
  Register #(.width(16)) register_8 (
    .D(demultiplexer_2_out7), .en(demultiplexer_1_out7), .Q(register_8_q), .clk(clk), .clr(clr));
  Register #(.width(16)) register_9 (
    .D(demultiplexer_2_out8), .en(demultiplexer_1_out8), .Q(register_9_q), .clk(clk), .clr(clr));
  Register #(.width(16)) register_10 (
    .D(demultiplexer_2_out9), .en(demultiplexer_1_out9), .Q(register_10_q), .clk(clk), .clr(clr));
  Register #(.width(16)) register_11 (
    .D(demultiplexer_2_out10), .en(demultiplexer_1_out10), .Q(register_11_q), .clk(clk), .clr(clr));
  Register #(.width(16)) register_12 (
    .D(demultiplexer_2_out11), .en(demultiplexer_1_out11), .Q(register_12_q), .clk(clk), .clr(clr));
  Register #(.width(16)) register_13 (
    .D(demultiplexer_2_out12), .en(demultiplexer_1_out12), .Q(register_13_q), .clk(clk), .clr(clr));
  Register #(.width(16)) register_14 (
    .D(demultiplexer_2_out13), .en(demultiplexer_1_out13), .Q(register_14_q), .clk(clk), .clr(clr));
  Register #(.width(16)) register_15 (
    .D(demultiplexer_2_out14), .en(demultiplexer_1_out14), .Q(register_15_q), .clk(clk), .clr(clr));
  Register #(.width(16)) register_16 (
    .D(demultiplexer_2_out15), .en(demultiplexer_1_out15), .Q(jumper), .clk(clk), .clr(clr));
  Multiplexer #(.select(4), .width(16)) multiplexer_1 (
    .in0(register_1_q), .in1(register_2_q), .in2(register_3_q), .in3(register_4_q), .in4(register_5_q),
    .in5(register_6_q), .in6(register_7_q), .in7(register_8_q), .in8(register_9_q), .in9(register_10_q),
    .in10(register_11_q), .in11(register_12_q), .in12(register_13_q), .in13(register_14_q),
    .in14(register_15_q), .in15(jumper), .out(data1), .sel(rs));  // open: en
  Multiplexer #(.select(4), .width(16)) multiplexer_2 (
    .in0(register_1_q), .in1(register_2_q), .in2(register_3_q), .in3(register_4_q), .in4(register_5_q),
    .in5(register_6_q), .in6(register_7_q), .in7(register_8_q), .in8(register_9_q), .in9(register_10_q),
    .in10(register_11_q), .in11(register_12_q), .in12(register_13_q), .in13(register_14_q),
    .in14(register_15_q), .in15(jumper), .out(data2), .sel(rt));  // open: en
endmodule

module ALU (
  input  [3:0] ALUop,
  input  [15:0] data1,
  input  [15:0] data2,
  input  [15:0] immed,
  input  [15:0] jumper,
  output [15:0] out,
  output zero
);

  Multiplexer #(.select(4), .width(16)) multiplexer_1 (
    .out(out), .sel(ALUop));  // open: in0, in1, in2, in3, in4, in5, in6, in7, in8, in9, in10, in11, in12, in13, in14, in15, en
  and and_1 (zero, ~out[0], ~out[1], ~out[2], ~out[3], ~out[4], ~out[5], ~out[6], ~out[7], ~out[8], ~out[9], ~out[10], ~out[11], ~out[12], ~out[13], ~out[14], ~out[15]);  // AND_Gate

  // Other names for the same wires on the sheet: op[3:0] = ALUop
endmodule

module ROM (
  input  [15:0] Address,
  input  gt,
  input  clk,
  input  clr,
  output [15:0] Instruction
);

  wire adder_1_cout, or_1_out;
  wire [15:0] adder_1_out, multiplexer_1_out, PC_q;

  Multiplexer #(.width(16)) multiplexer_1 (
    .in0(adder_1_out), .in1(Address), .out(multiplexer_1_out), .sel(gt));  // open: en
  Register #(.width(16)) PC (.D(multiplexer_1_out), .Q(PC_q), .clk(clk), .clr(or_1_out));  // open: en
  or or_1 (or_1_out, adder_1_cout, clr);
  Adder #(.width(16)) adder_1 (.a(16'h1), .b(PC_q), .out(adder_1_out), .cout(adder_1_cout));  // open: cin
  ROM_part #(.addrWidth(16), .dataWidth(16)) rom_1 (.addr(PC_q), .data(Instruction));  // open: sel
endmodule

module MEM (
  input  [15:0] Address,
  input  sw,
  input  clk,
  input  lw,
  input  clr,
  input  [15:0] DataIn,
  output [15:0] DataOut
);

  RAM #(.addrWidth(16), .dataWidth(16), .bus("separate")) ram_1 (
    .addr(Address), .din(DataIn), .data(DataOut), .str(sw), .sel(1'b1), .clk(clk), .ld(lw), .clr(clr));
endmodule

module Control_Logic (
  input  [3:0] op,
  output j,
  output b,
  output ldMem,
  output strMem,
  output strReg
);

  wire and_5_out, and_6_out;

  and and_1 (j, op[3], ~op[1]);  // AND_Gate
  and and_2 (b, op[3], ~op[1], ~op[0]);  // AND_Gate
  and and_3 (ldMem, op[3], op[1], ~op[0]);  // AND_Gate
  and and_4 (strMem, op[3], op[1], op[0]);
  and and_5 (and_5_out, ~op[3], op[0]);  // AND_Gate
  and and_6 (and_6_out, op[1], ~op[0]);  // AND_Gate
  or or_1 (strReg, and_5_out, and_6_out, op[2]);
endmodule
