// Logisim project sketch.circ as structural Verilog
module main (
);

  wire button_out, clk, clock_1_out, clr, lw, on, sw;
  wire [7:0] cpu_1_ram_address, cpu_1_ram_dbus, undriven;

  Clock clock_1 (.out(clock_1_out));
  switch switch_1 (.in_1(button_out), .out_2(on));
  Button button (.out(button_out));
  Button u_clr (.out(clr));
  assign clk = on ? clock_1_out : 1'bz;  // Controlled_Buffer controlled_buffer_1
  CPU cpu_1 (.clr(clr), .clk(clk), .Data_In(undriven), .RAM_dbus(cpu_1_ram_dbus), .RAM_Address(cpu_1_ram_address));
  RAM #(.bus("separate")) ram_1 (
    .addr(cpu_1_ram_address), .din(undriven), .data(cpu_1_ram_dbus), .str(sw), .sel(on), .clk(clk), .ld(lw),
    .clr(clr));
endmodule

module CPU (
  input  clr,
  input  clk,
  input  [7:0] Data_In,
  output [7:0] RAM_dbus,
  output [7:0] RAM_Address
);

  Regs regs_1 ();  // open: RegSelect, DataIn, str, clk, clr, DataOut
  ALU alu_1 ();
  ALU_Control alu_control_1 ();
endmodule

module PC (
  input  in_1,
  output [7:0] out_2
);

  wire clock_1_out;
  wire [7:0] adder_1_out, register_1_q;

  Clock clock_1 (.out(clock_1_out));
  Register register_1 (.D(adder_1_out), .Q(register_1_q), .clk(clock_1_out), .clr(in_1));  // open: en
  Adder adder_1 (.a(8'h1), .b(register_1_q), .out(adder_1_out));  // open: cin, cout
  ROM rom_1 (.addr(register_1_q), .data(out_2), .sel(1'b1));

  // Notes on the sheet:
  //   contents of rom_1 (hex, n*v repeats v):
  //   aa ff
endmodule

module Regs (
  input  [2:0] RegSelect,
  input  [7:0] DataIn,
  input  str,
  input  clk,
  input  clr,
  output [7:0] DataOut
);

  wire [7:0] demultiplexer_1_out0, demultiplexer_1_out1, demultiplexer_1_out2, demultiplexer_1_out3,
       demultiplexer_1_out4, demultiplexer_1_out5, demultiplexer_1_out6, demultiplexer_1_out7, register_1_q,
       register_2_q, register_3_q, register_4_q, register_5_q, register_6_q, register_7_q, register_8_q;

  Demultiplexer #(.select(3), .width(8)) demultiplexer_1 (
    .out0(demultiplexer_1_out0), .out1(demultiplexer_1_out1), .out2(demultiplexer_1_out2),
    .out3(demultiplexer_1_out3), .out4(demultiplexer_1_out4), .out5(demultiplexer_1_out5),
    .out6(demultiplexer_1_out6), .out7(demultiplexer_1_out7), .in(DataIn), .sel(RegSelect));  // open: en
  Register register_1 (.D(demultiplexer_1_out0), .en(str), .Q(register_1_q), .clk(clk), .clr(clr));
  Register register_2 (.D(demultiplexer_1_out1), .en(str), .Q(register_2_q), .clk(clk), .clr(clr));
  Register register_3 (.D(demultiplexer_1_out2), .en(str), .Q(register_3_q), .clk(clk), .clr(clr));
  Register register_4 (.D(demultiplexer_1_out3), .en(str), .Q(register_4_q), .clk(clk), .clr(clr));
  Register register_5 (.D(demultiplexer_1_out4), .en(str), .Q(register_5_q), .clk(clk), .clr(clr));
  Register register_6 (.D(demultiplexer_1_out5), .en(str), .Q(register_6_q), .clk(clk), .clr(clr));
  Register register_7 (.D(demultiplexer_1_out6), .en(str), .Q(register_7_q), .clk(clk), .clr(clr));
  Register register_8 (.D(demultiplexer_1_out7), .en(str), .Q(register_8_q), .clk(clk), .clr(clr));
  Multiplexer #(.select(3), .width(8)) multiplexer_1 (
    .in0(register_1_q), .in1(register_2_q), .in2(register_3_q), .in3(register_4_q), .in4(register_5_q),
    .in5(register_6_q), .in6(register_7_q), .in7(register_8_q), .out(DataOut), .sel(RegSelect));  // open: en

  // Other names for the same wires on the sheet: RS[2:0] = RegSelect
endmodule

module ALU (
);

  wire [7:0] ram_1_data, undriven, undriven_2;

  RAM #(.bus("separate")) ram_1 (.addr(undriven), .din(undriven_2), .data(ram_1_data));  // open: str, sel, clk, ld, clr
endmodule

module switch (
  input  in_1,
  output out_2
);

  wire d_ff_1_qn;

  D_Flip_Flop d_ff_1 (.clk(in_1), .D(d_ff_1_qn), .Q(out_2), .Qn(d_ff_1_qn));  // open: preset, en, reset
endmodule
